# Fritzing sketch perfboard layout (saved by Fritzing 0.9.4)
perfboards: 1

parts:
  U1 = LM 358 Dual Op-Amp [package="DIP8 [THT]"]
  D1 = Rectifier Diode [part_number=1N4001 package="300 mil [THT]"]
  R1 = Resistor [tolerance=±5% resistance=10k package=THT]
  R2 = Resistor [tolerance=±5% resistance=470k package=THT]
  R3 = Resistor [tolerance=±5% resistance=10k package=THT]
  R4 = Resistor [tolerance=±5% resistance=10k package=THT]
  J1 = Screw terminal - 2 pins [package=THT]
  J2 = female pin header, 2 pins [form="♀ (female)"]
  J3 = female pin header, 3 pins [form="♀ (female)"]

nets:
  N1: U1.connector0, U1.connector5, D1.anode, R1.Pin_1, J2.pin1
  N2: U1.connector1, R1.Pin_0, R2.Pin_1
  N3: U1.connector2, R3.Pin_1, R4.Pin_1
  GND: U1.connector3, R4.Pin_0, J1.pin2, J2.pin2, J3.pin3
  3.3V: U1.connector4, R3.Pin_0, J3.pin2
  N4: U1.connector6, D1.cathode
  5V: U1.connector7, J3.pin1
  N5: R2.Pin_0, J1.pin1
